# Fritzing sketch Breadboard (saved by Fritzing 1.0.4)
breadboards: 1

parts:
  M1 = M5-STAMP-C3U [part_number=M5-STAMP-C3U]
  LED1 = LED - 3mm [color="Yellow (595nm)" current=30mA package="3 mm [THT]"]
  LED2 = LED - 3mm [color="Green (570nm)" current=0.030A package="3 mm [THT]"]

nets:
  N1: M1.7, M1.8, M1.5V#19
  N2: M1.10, M1.5V#17, LED1.cathode, LED1.anode, LED2.cathode, LED2.anode
